// Digital circuit MEF_MLR.dig as structural Verilog
module MEF_MLR (
  input  [2:0] PROG,
  input  CHEIO,
  input  TAMPA,
  input  LIGA,
  input  CLK,
  input  RESET,
  input  [3:0] CK,
  output ENCHER,
  output ESVAZIAR,
  output AGITAR,
  output GIRAR,
  output SUSPENDER
);
endmodule
