// Digital circuit Principal.dig as structural Verilog
module Principal (
  input  CLK,
  input  [1:0] PROG,
  input  CHEIO,
  input  TAMPA,
  input  LIGA,
  output ENCHER,
  output ESVAZIAR,
  output AGITAR,
  output GIRAR
);

  wire CONT_ovf, mlr_modularizada_1_suspender, RESET_out;

  Reset #(.invertOutput("false")) RESET (.out(RESET_out));
  Counter #(.Bits(4)) CONT (.en(mlr_modularizada_1_suspender), .C(CLK), .clr(RESET_out), .ovf(CONT_ovf));  // open: out
  mlr_modularizada mlr_modularizada_1 (
    .PROG(PROG), .CHEIO(CHEIO), .TAMPA(TAMPA), .LIGA(LIGA), .CLK(CLK), .RESET(RESET_out), .CK_OVF(CONT_ovf),
    .ENCHER(ENCHER), .ESVAZIAR(ESVAZIAR), .AGITAR(AGITAR), .GIRAR(GIRAR),
    .SUSPENDER(mlr_modularizada_1_suspender));

  // Notes on the sheet:
  //   ERRO :QUANDO A TAMPA É LEVANTADA A OPERAÇÃO CONTINUA
endmodule

/* Test case MLR:
CLK  LIGA   PROG   CHEIO  TAMPA  ENCHER   ESVAZIAR   AGITAR  GIRAR
C     0      X      0      0	  0	   0	      0	      0
*/
