// Digital circuit caixinhaD1.dig as structural Verilog
module caixinhaD1 (
  input  C,
  input  CLK,
  input  L,
  input  T,
  input  Z_0_n,
  input  Z_1_n,
  input  Z_2_n,
  input  Z_3_n,
  output D1
);

  wire and_1_out, and_2_out, and_3_out, and_4_out, and_5_out, and_6_out, and_7_out, not_1_out, not_2_out,
       not_3_out, not_4_out, not_5_out, not_6_out, not_7_out, not_8_out;

  not not_1 (not_1_out, Z_0_n);
  not not_2 (not_2_out, Z_1_n);
  not not_3 (not_3_out, Z_2_n);
  not not_4 (not_4_out, Z_3_n);
  not not_5 (not_5_out, T);
  not not_6 (not_6_out, L);
  not not_7 (not_7_out, CLK);
  not not_8 (not_8_out, C);
  and and_1 (and_1_out, C, L, not_5_out, Z_0_n, not_2_out, not_3_out);
  and and_2 (and_2_out, C, L, not_5_out, Z_0_n, Z_2_n, not_4_out);
  and and_3 (and_3_out, CLK, L, not_5_out, Z_0_n, not_2_out, Z_2_n, Z_3_n);
  and and_4 (and_4_out, not_7_out, L, Z_1_n, not_3_out);
  and and_5 (and_5_out, not_7_out, L, Z_1_n, Z_3_n);
  and and_6 (and_6_out, L, T, Z_1_n);
  and and_7 (and_7_out, L, not_1_out, Z_1_n);
  or or_1 (D1, and_1_out, and_2_out, and_3_out, and_4_out, and_5_out, and_6_out, and_7_out);
endmodule
