// Digital circuit circuitinho_passa.dig as structural Verilog
module circuitinho_passa (
  input  OVF,
  input  C,
  output PASSA
);

  wire and_1_out, and_2_out, and_3_out, not_1_out, not_2_out, or_1_out, Z_0_n, Z_1_n;

  not not_1 (not_1_out, OVF);
  not not_2 (not_2_out, Z_1_n);
  and and_1 (and_1_out, OVF, Z_0_n);
  and and_2 (and_2_out, not_1_out, Z_1_n);
  and and_3 (and_3_out, not_1_out, not_2_out);
  and and_4 (PASSA, OVF, Z_0_n);
  or or_1 (or_1_out, and_1_out, and_2_out);
  D_FF #(.Default(1)) u_Z_1_n (.D(or_1_out), .C(C), .Q(Z_1_n));  // open: nQ
  D_FF u_Z_0_n (.D(and_3_out), .C(C), .Q(Z_0_n));  // open: nQ

  // Notes on the sheet:
  //   C: Hz: 2
endmodule
