// Digital circuit circuito_passa.dig as structural Verilog
module circuito_passa (
  input  C,
  input  en,
  input  CK,
  output P
);

  wire and_1_out, and_2_out, and_3_out, l_2_out, l_3_out, l_out, not_1_out, not_2_out, or_1_out, OVF, Z_0_n,
       Z_1_n;

  Counter l (.en(en), .C(CK), .clr(1'b0), .out(l_out));  // open: ovf
  Counter l_2 (.en(en), .C(l_out), .clr(1'b0), .out(l_2_out));  // open: ovf
  Counter l_3 (.en(en), .C(l_2_out), .clr(1'b0), .out(l_3_out));  // open: ovf
  Counter l_4 (.en(en), .C(l_3_out), .clr(1'b0), .ovf(OVF));  // open: out
  not not_1 (not_1_out, OVF);
  not not_2 (not_2_out, Z_1_n);
  and and_1 (and_1_out, OVF, Z_0_n);
  and and_2 (and_2_out, not_1_out, Z_1_n);
  and and_3 (and_3_out, not_1_out, not_2_out);
  and and_4 (P, OVF, Z_0_n);
  or or_1 (or_1_out, and_1_out, and_2_out);
  D_FF #(.Default(1)) u_Z_1_n (.D(or_1_out), .C(C), .Q(Z_1_n));  // open: nQ
  D_FF u_Z_0_n (.D(and_3_out), .C(C), .Q(Z_0_n));  // open: nQ

  // Notes on the sheet:
  //   C: Hz: 2
endmodule
