// Digital circuit clock_mlr.dig as structural Verilog
module clock_mlr (
  input  Q0,
  input  Q1,
  input  Q2,
  input  Q3,
  input  T,
  output Hold
);

  wire multiplexer_1_out;

  Multiplexer #(.Selector_Bits(4)) multiplexer_1 (
    .sel({Q3, Q2, Q1, Q0}), .in_0(1'b0), .in_1(1'b0), .in_2(1'b1), .in_3(1'b1), .in_4(1'b0), .in_5(1'b0),
    .in_6(1'b1), .in_7(1'b0), .in_8(1'b1), .in_9(1'b0), .in_10(1'b1), .in_11(1'b0), .in_12(1'b0),
    .in_13(1'b1), .in_14(1'b0), .in_15(1'b1), .out(multiplexer_1_out));
  and and_1 (Hold, multiplexer_1_out, ~T);  // And
endmodule
