// Digital circuit mlr_modularizada.dig as structural Verilog
module mlr_modularizada (
  input  [1:0] PROG,
  input  CHEIO,
  input  TAMPA,
  input  LIGA,
  input  CLK,
  input  RESET,
  input  CK_OVF,
  output ENCHER,
  output ESVAZIAR,
  output AGITAR,
  output GIRAR,
  output SUSPENDER
);

  wire caixinhad0_1_d0, caixinhad1_1_d1, caixinhad2_1_d2, caixinhad3_1_d3, Z_0_n, Z_1_n, Z_2_n, Z_3_n;

  caixinhaD3 caixinhad3_1 (
    .C(CHEIO), .CLK(CK_OVF), .L(LIGA), .P0(PROG[0]), .P1(PROG[1]), .T(TAMPA), .Z_0_n(Z_0_n), .Z_1_n(Z_1_n),
    .Z_2_n(Z_2_n), .Z_3_n(Z_3_n), .D3(caixinhad3_1_d3));
  caixinhaD2 caixinhad2_1 (
    .C(CHEIO), .CLK(CK_OVF), .L(LIGA), .P0(PROG[0]), .P1(PROG[1]), .T(TAMPA), .Z_0_n(Z_0_n), .Z_1_n(Z_1_n),
    .Z_2_n(Z_2_n), .Z_3_n(Z_3_n), .D2(caixinhad2_1_d2));
  caixinhaD1 caixinhad1_1 (
    .C(CHEIO), .CLK(CK_OVF), .L(LIGA), .T(TAMPA), .Z_0_n(Z_0_n), .Z_1_n(Z_1_n), .Z_2_n(Z_2_n), .Z_3_n(Z_3_n),
    .D1(caixinhad1_1_d1));
  caixinhaD0 caixinhad0_1 (
    .C(CHEIO), .CLK(CK_OVF), .L(LIGA), .P0(PROG[0]), .P1(PROG[1]), .T(TAMPA), .Z_0_n(Z_0_n), .Z_1_n(Z_1_n),
    .Z_2_n(Z_2_n), .Z_3_n(Z_3_n), .D0(caixinhad0_1_d0));
  saidaAGI saidaagi_1 (
    .C(CHEIO), .CLK(CK_OVF), .L(LIGA), .P0(PROG[0]), .P1(PROG[1]), .T(TAMPA), .Z_0_n(Z_0_n), .Z_1_n(Z_1_n),
    .Z_2_n(Z_2_n), .Z_3_n(Z_3_n), .agi(AGITAR));
  saidaEN saidaen_1 (
    .C(CHEIO), .CLK(CK_OVF), .L(LIGA), .P0(PROG[0]), .P1(PROG[1]), .T(TAMPA), .Z_0_n(Z_0_n), .Z_1_n(Z_1_n),
    .Z_2_n(Z_2_n), .Z_3_n(Z_3_n), .en(ENCHER));
  saidaES saidaes_1 (
    .C(CHEIO), .CLK(CK_OVF), .L(LIGA), .P0(PROG[0]), .P1(PROG[1]), .T(TAMPA), .Z_0_n(Z_0_n), .Z_1_n(Z_1_n),
    .Z_2_n(Z_2_n), .Z_3_n(Z_3_n), .es(ESVAZIAR));
  saidaGI saidagi_1 (
    .C(CHEIO), .CLK(CK_OVF), .L(LIGA), .P0(PROG[0]), .P1(PROG[1]), .T(TAMPA), .Z_0_n(Z_0_n), .Z_1_n(Z_1_n),
    .Z_2_n(Z_2_n), .Z_3_n(Z_3_n), .gi(GIRAR));
  clock_mlr clock_mlr_1 (.Q0(Z_0_n), .Q1(Z_1_n), .Q2(Z_2_n), .Q3(Z_3_n), .T(TAMPA), .Hold(SUSPENDER));
  D_FF u_Z_3_n (.D(caixinhad3_1_d3), .C(CLK), .Q(Z_3_n));  // open: nQ
  D_FF u_Z_2_n (.D(caixinhad2_1_d2), .C(CLK), .Q(Z_2_n));  // open: nQ
  D_FF u_Z_1_n (.D(caixinhad1_1_d1), .C(CLK), .Q(Z_1_n));  // open: nQ
  D_FF u_Z_0_n (.D(caixinhad0_1_d0), .C(CLK), .Q(Z_0_n));  // open: nQ
endmodule
