// Digital circuit saidaGI.dig as structural Verilog
module saidaGI (
  input  C,
  input  CLK,
  input  L,
  input  P0,
  input  P1,
  input  T,
  input  Z_0_n,
  input  Z_1_n,
  input  Z_2_n,
  input  Z_3_n,
  output gi
);

  wire and_1_out, and_2_out, and_3_out, and_4_out, and_5_out, and_6_out, not_1_out, not_2_out, not_3_out,
       not_4_out, not_5_out, not_6_out, not_7_out, not_8_out, not_9_out, not_10_out;

  not not_1 (not_1_out, Z_0_n);
  not not_2 (not_2_out, Z_1_n);
  not not_3 (not_3_out, Z_2_n);
  not not_4 (not_4_out, Z_3_n);
  not not_5 (not_5_out, T);
  not not_6 (not_6_out, P1);
  not not_7 (not_7_out, P0);
  not not_8 (not_8_out, L);
  not not_9 (not_9_out, CLK);
  not not_10 (not_10_out, C);
  and and_1 (and_1_out, not_10_out, L, not_5_out, Z_0_n, Z_1_n, Z_2_n, not_4_out);
  and and_2 (and_2_out, not_10_out, L, not_5_out, not_1_out, Z_1_n, Z_2_n, Z_3_n);
  and and_3 (and_3_out, not_9_out, L, not_1_out, not_2_out, not_3_out, Z_3_n);
  and and_4 (and_4_out, not_9_out, L, Z_0_n, Z_1_n, Z_2_n, Z_3_n);
  and and_5 (and_5_out, L, T, not_1_out, not_2_out, not_3_out, Z_3_n);
  and and_6 (and_6_out, L, T, Z_0_n, Z_1_n, Z_2_n, Z_3_n);
  or or_1 (gi, and_1_out, and_2_out, and_3_out, and_4_out, and_5_out, and_6_out);
endmodule
